# Fritzing sketch Fritzing (saved by Fritzing 0.8.7b)
breadboards: 1

parts:
  Part1 = Photon
  LED1 = LED - 5mm [color="Red (633nm)" package="5 mm [THT]"]
  R1 = Resistor [tolerance=±5% resistance=220 package=THT]
  DHT1 = DHT11 Humitidy and Temperature Sensor
  Water_Level_Sensor1 = Water Level Sensor

nets:
  N1: Part1.A2, Water_Level_Sensor1.SIG
  GND: Part1.GND, R1.Pin_1, DHT1.GND, Water_Level_Sensor1.GND
  N2: Part1.D2, DHT1.DATA
  N3: Part1.D5, LED1.anode
  3V3: Part1.3V3, DHT1.VDD, Water_Level_Sensor1.VCC
  N4: LED1.cathode, R1.Pin_0

custom parts:
  DHT11 Humitidy and Temperature Sensor: DHT11 Humidity and Temperature Sensor
  Water Level Sensor: A water level sensor. This sensor operates at 3V to 5V. The Sig (signal) pin outputs an analogue signal that is in proportion to the amount of water in contact with the sensor.
